// Logisim project Timer Interrupt.circ as structural Verilog: 3 circuits, main circuit main
module main (
  input  [2:0] FC,
  input  [3:0] Addr,
  input  nDS,
  input  nReset,
  input  [7:0] ADDR_2,
  input  [7:0] PortSel,
  output nAVEC,
  output Q1,
  output nIRQ,
  output Q0,
  output RCO,
  output nY
);

  wire _32kHz_out, and_1_out, and_2_out, and_3_out, and_4_out, and_5_out, and_6_out, and_7_out, n7474_1_nq,
       n7474_2_nq, n74688_2_out_4, nand_1_out, nand_2_out, nand_3_out, nand_4_out, or_1_out, or_2_out,
       pull_resistor_1_node;

  Clock _32kHz (.out(_32kHz_out));
  _74688 u_74688_1 (.A({1'b1, Addr, FC}), .B({8{1'b1}}), .nEN(nDS), .out_4(nY));
  _74688 u_74688_2 (.A(ADDR_2), .B(PortSel), .nEN(nDS), .out_4(n74688_2_out_4));
  nand nand_1 (nand_1_out, nand_2_out, and_7_out);
  nand nand_2 (nand_2_out, n74688_2_out_4, n74688_2_out_4);
  and and_1 (and_1_out, nand_1_out, and_2_out);
  and and_2 (and_2_out, nReset, nand_3_out);
  nand nand_3 (nand_3_out, nDS, and_6_out);
  and and_3 (and_3_out, Q0, RCO);
  Pull_Resistor #(.pull(1)) pull_resistor_1 (.node(pull_resistor_1_node));
  _7474 u_7474_1 (.D(or_1_out), .Clk(_32kHz_out), .Q(Q1), .nQ(n7474_1_nq), .nS(pull_resistor_1_node), .nR(and_1_out));
  _7474 u_7474_2 (.D(and_4_out), .Clk(_32kHz_out), .Q(Q0), .nQ(n7474_2_nq), .nS(nand_1_out), .nR(and_2_out));
  Counter #(.width(4), .max('hf)) counter_1 (
    .D(4'b0000), .count(and_5_out), .carry(RCO), .clk(_32kHz_out));  // open: load, Q, clr
  and and_4 (and_4_out, or_2_out, Q0);
  or or_1 (or_1_out, and_3_out, Q1);
  or or_2 (or_2_out, n7474_1_nq, nY);
  and and_5 (and_5_out, n7474_1_nq, Q0);
  and and_6 (and_6_out, n7474_2_nq, Q1);
  and and_7 (and_7_out, n7474_2_nq, n7474_1_nq);
  nand nand_4 (nand_4_out, Q1, n7474_2_nq);
  buf buffer_1 (nAVEC, nand_4_out);
  buf buffer_2 (nIRQ, n7474_1_nq);
endmodule

module _74688 (
  input  [7:0] A,
  input  [7:0] B,
  input  nEN,
  output out_4
);

  wire comparator_1_eq, not_1_out;

  Comparator comparator_1 (.a(A), .b(B), .eq(comparator_1_eq));  // open: gt, lt
  not not_1 (not_1_out, comparator_1_eq);
  or or_1 (out_4, not_1_out, nEN);
endmodule

module _7474 (
  input  nS,
  input  D,
  input  Clk,
  input  nR,
  output Q,
  output nQ
);

  wire not_1_out, not_2_out;

  D_Flip_Flop d_ff_1 (.clk(Clk), .D(D), .Q(Q), .Qn(nQ), .preset(not_1_out), .reset(not_2_out));  // open: en
  not not_1 (not_1_out, nS);
  not not_2 (not_2_out, nR);
endmodule
